// Digital circuit 4-bit_register.dig as structural Verilog
module _4_bit_register (
  input  [3:0] Data,
  input  Clock,
  input  Clear,
  input  R_W,
  output [3:0] Out
);

  wire [3:0] and_1_out;
  wire [3:3] not_1_out;

  not not_1 (not_1_out[3], Clear);
  assign and_1_out = Data & {4{not_1_out[3]}};  // And and_1, 4 bits wide
  _1_bit_memory_cell__D_flip_flop _1_bit_memory_cell__d_flip_flop_1 (
    .D(and_1_out[0]), .Clock(Clock), .R_W(R_W), .Q(Out[0]));
  _1_bit_memory_cell__D_flip_flop _1_bit_memory_cell__d_flip_flop_2 (
    .D(and_1_out[1]), .Clock(Clock), .R_W(R_W), .Q(Out[1]));
  _1_bit_memory_cell__D_flip_flop _1_bit_memory_cell__d_flip_flop_3 (
    .D(and_1_out[2]), .Clock(Clock), .R_W(R_W), .Q(Out[2]));
  _1_bit_memory_cell__D_flip_flop _1_bit_memory_cell__d_flip_flop_4 (
    .D(and_1_out[3]), .Clock(Clock), .R_W(R_W), .Q(Out[3]));
endmodule
