// Digital circuit 4bit_ALU.dlogic.dig as structural Verilog
module _4bit_ALU_dlogic (
  input  [3:0] A,
  input  [3:0] B,
  input  [2:0] Control,
  input  zero,
  input  [1:0] MOV,
  output [3:0] Result,
  output Zero_Flag,
  output overflow,
  output Less_Than_Flag,
  output underflow
);

  wire _4bit_full_adder_1_p4, _4bit_logicoperations_1_p3, _4bit_logicoperations_1_p4,
       _4bit_logicoperations_1_p5, _4bit_subtractor_1_p4, not_2_out, or_1_out;
  wire [3:0] and_1_out;
  wire [3:3] not_1_out;
  wire [4:0] _4bit_setlessthanflag_1_result;

  or or_1 (or_1_out, MOV[0], MOV[1]);
  not not_1 (not_1_out[3], or_1_out);
  assign and_1_out = B & {4{not_1_out[3]}};  // And and_1, 4 bits wide
  not not_2 (not_2_out, zero);
  // _4bit_full_adder _4bit_full_adder_1: pin names not known; wires that end beside it: zero, A, and_1_out, _4bit_full_adder_1_p4, overflow
  // _4bit_subtractor _4bit_subtractor_1: pin names not known; wires that end beside it: A, and_1_out, not_2_out, _4bit_subtractor_1_p4, underflow
  // _4bit_logicOperations _4bit_logicoperations_1: pin names not known; wires that end beside it: A, and_1_out, _4bit_logicoperations_1_p3, _4bit_logicoperations_1_p4, _4bit_logicoperations_1_p5
  _4bit_setLessThanFlag _4bit_setlessthanflag_1 (
    .A(A), .B(and_1_out), .zero(zero), .Result(_4bit_setlessthanflag_1_result));
  // _4bit_multiplexer_6x2 _4bit_multiplexer_6x2_1: pin names not known; wires that end beside it: Control, _4bit_full_adder_1_p4, _4bit_subtractor_1_p4, _4bit_logicoperations_1_p3, _4bit_logicoperations_1_p4, _4bit_logicoperations_1_p5, _4bit_setlessthanflag_1_result, Result, Less_Than_Flag
  // _4bit_zeroflag _4bit_zeroflag_1: pin names not known; wires that end beside it: Result, Zero_Flag
endmodule
