// Digital circuit 4bit_Instruction_Register.dig as structural Verilog
module _4bit_Instruction_Register (
  input  [3:0] Data,
  input  Clock,
  input  Clear,
  input  R_W,
  output [3:0] Address_Bus,
  output [2:0] ALU_Op
);

  _4_bit_register IR (.Data(Data), .Clock(Clock), .Clear(Clear), .R_W(R_W), .Out(Address_Bus));
  IR_decoder ir_decoder_1 (.IR(Address_Bus), .ALU(ALU_Op));
endmodule
