// Digital circuit 4bit_Processor.dlogic.dig as structural Verilog
module _4bit_Processor_dlogic (
);

  _4bit_ALU_dlogic _4bit_alu_dlogic_1 ();  // open: A, B, Control, zero, Result, Zero_Flag, overflow, Less_Than_Flag, underflow
  _4bit_Instruction_Register _4bit_instruction_register_1 ();  // open: Data, Clock, Clear, R_W, Address_Bus, ALU_Op
  _4bit_registerFileALU _4bit_registerfilealu_1 ();  // open: Write_Register, Read_Register_1, Read_Register_2, Write_Data, Clock, Read_Data_1, Read_data_2
  CU cu_1 ();  // open: Opcode__IR, Zero_flag, reset, clock, ALU_Op, Read_Reg_1, Read_Reg_2, Write_Reg, Write_Enabled, Immediate_Load, Increment, Fetch_Enable
  programCounter programcounter_1 ();  // open: Load, Increment, Clock, R_W, Clear, Address_bus, Out_of_range
endmodule
