// Digital circuit 4bit_registerFileALU.dig as structural Verilog
module _4bit_registerFileALU (
  input  [1:0] Write_Register,
  input  [1:0] Read_Register_1,
  input  [1:0] Read_Register_2,
  input  [3:0] Write_Data,
  input  Clock,
  input  Clear,
  input  R_W,
  output [3:0] Read_Data_1,
  output [3:0] Read_data_2
);

  wire demultiplexer_2_out_0, demultiplexer_2_out_1, demultiplexer_2_out_2, demultiplexer_2_out_3;
  wire [3:0] _4_bit_register_1_out, _4_bit_register_2_out, _4_bit_register_3_out, _4_bit_register_4_out,
       demultiplexer_1_out_0, demultiplexer_1_out_1, demultiplexer_1_out_2, demultiplexer_1_out_3;

  Demultiplexer #(.Selector_Bits(2), .Bits(4)) demultiplexer_1 (
    .sel(Write_Register), .in(Write_Data), .out_0(demultiplexer_1_out_0), .out_1(demultiplexer_1_out_1),
    .out_2(demultiplexer_1_out_2), .out_3(demultiplexer_1_out_3));
  Demultiplexer #(.Selector_Bits(2)) demultiplexer_2 (
    .sel(Write_Register), .in(R_W), .out_0(demultiplexer_2_out_0), .out_1(demultiplexer_2_out_1),
    .out_2(demultiplexer_2_out_2), .out_3(demultiplexer_2_out_3));
  _4_bit_register _4_bit_register_1 (
    .Data(demultiplexer_1_out_0), .Clock(Clock), .Clear(Clear), .R_W(demultiplexer_2_out_0),
    .Out(_4_bit_register_1_out));
  _4_bit_register _4_bit_register_2 (
    .Data(demultiplexer_1_out_1), .Clock(Clock), .Clear(Clear), .R_W(demultiplexer_2_out_1),
    .Out(_4_bit_register_2_out));
  _4_bit_register _4_bit_register_3 (
    .Data(demultiplexer_1_out_2), .Clock(Clock), .Clear(Clear), .R_W(demultiplexer_2_out_2),
    .Out(_4_bit_register_3_out));
  _4_bit_register _4_bit_register_4 (
    .Data(demultiplexer_1_out_3), .Clock(Clock), .Clear(Clear), .R_W(demultiplexer_2_out_3),
    .Out(_4_bit_register_4_out));
  Multiplexer #(.Selector_Bits(2), .Bits(4)) multiplexer_1 (
    .sel(Read_Register_1), .in_0(_4_bit_register_1_out), .in_1(_4_bit_register_2_out),
    .in_2(_4_bit_register_3_out), .in_3(_4_bit_register_4_out), .out(Read_Data_1));
  Multiplexer #(.Selector_Bits(2), .Bits(4)) multiplexer_2 (
    .sel(Read_Register_2), .in_0(_4_bit_register_1_out), .in_1(_4_bit_register_2_out),
    .in_2(_4_bit_register_3_out), .in_3(_4_bit_register_4_out), .out(Read_data_2));
endmodule
