// Digital circuit 4bit_setLessThanFlag.dig as structural Verilog
module _4bit_setLessThanFlag (
  input  [3:0] A,
  input  [3:0] B,
  input  zero,
  output [4:0] Result
);

  wire and_1_out, and_2_out, and_3_out, and_4_out, not_1_out, not_2_out, not_3_out, not_4_out, xor_1_out,
       xor_2_out, xor_3_out, xor_4_out;

  xor xor_1 (xor_1_out, A[0], B[0]);
  not not_1 (not_1_out, A[0]);
  xor xor_2 (xor_2_out, A[1], B[1]);
  xor xor_3 (xor_3_out, A[2], B[2]);
  xor xor_4 (xor_4_out, A[3], B[3]);
  and and_1 (and_1_out, xor_1_out, not_1_out);
  and and_2 (and_2_out, xor_2_out, not_2_out);
  not not_2 (not_2_out, A[1]);
  and and_3 (and_3_out, xor_3_out, not_3_out);
  not not_3 (not_3_out, A[2]);
  and and_4 (and_4_out, xor_4_out, not_4_out);
  not not_4 (not_4_out, A[3]);
  or or_1 (Result[4], and_1_out, and_2_out, and_3_out, and_4_out);

  assign Result[3:0] = {{3{zero}}, Result[4]};
endmodule
