// Digital circuit ALUAssignment3Step2.dig as structural Verilog
module ALUAssignment3Step2 (
  input  [3:0] Data_Input_A,
  input  [3:0] Data_Input_B,
  input  [3:0] ALU_Operation_Select,
  input  Clock,
  output [3:0] ALU_Result
);

  wire multiplexer_1_out;

  Multiplexer multiplexer_1 (.in_0(ALU_Operation_Select[0]), .out(multiplexer_1_out));  // open: sel, in_1
  // _4bit_registerFileALU _4bit_registerfilealu_1: pin names not known; wires that end beside it: multiplexer_1_out, ALU_Result, Clock, Data_Input_A, Data_Input_B
  // Pins of 1 and 4 bits meet at ALU_Operation_Select
endmodule
