// Digital circuit ALU_DataPathAssembly.dig as structural Verilog
module ALU_DataPathAssembly (
  input  [1:0] Data_Input_A,
  input  [1:0] Data_Input_B,
  input  [2:0] ALU_Operation_Select,
  input  Clock,
  input  [1:0] Write_Register,
  input  Clear,
  input  R_W,
  output [3:0] ALU_Result,
  output Zero_Flag,
  output Less_Than_Flag,
  output Over_Underflow
);

  wire _4bit_alu_dlogic_1_overflow, _4bit_alu_dlogic_1_underflow;
  wire [3:0] _4bit_registerfilealu_1_read_data_1, _4bit_registerfilealu_1_read_data_2;

  _4bit_ALU_dlogic _4bit_alu_dlogic_1 (
    .A(_4bit_registerfilealu_1_read_data_1), .B(_4bit_registerfilealu_1_read_data_2),
    .Control(ALU_Operation_Select), .zero(1'b0), .Result(ALU_Result), .Zero_Flag(Zero_Flag),
    .overflow(_4bit_alu_dlogic_1_overflow), .Less_Than_Flag(Less_Than_Flag),
    .underflow(_4bit_alu_dlogic_1_underflow));
  _4bit_registerFileALU _4bit_registerfilealu_1 (
    .Write_Register(Write_Register), .Read_Register_1(Data_Input_A), .Read_Register_2(Data_Input_B),
    .Write_Data(ALU_Result), .Clock(Clock), .Clear(Clear), .R_W(R_W),
    .Read_Data_1(_4bit_registerfilealu_1_read_data_1), .Read_data_2(_4bit_registerfilealu_1_read_data_2));
  or or_1 (Over_Underflow, _4bit_alu_dlogic_1_overflow, _4bit_alu_dlogic_1_underflow);
endmodule
