// Digital circuit CU.dig as structural Verilog
module CU (
  input  [3:0] Opcode__IR,
  input  Zero_flag,
  input  reset,
  input  clock,
  output [2:0] ALU_Op,
  output [1:0] Read_Reg_1,
  output [1:0] Read_Reg_2,
  output [1:0] Write_Reg,
  output Write_Enabled,
  output Immediate_Load,
  output Increment,
  output Fetch_Enable,
  output Zero_Flag_2,
  output [1:0] MOV,
  output Execute
);

  wire and_2_out, and_4_out, and_5_out, and_6_out, and_7_out, and_9_out, and_15_out,
       finitestatemachine_1_msb, not_2_out, not_3_out, not_4_out, not_5_out, not_6_out, not_7_out, not_8_out,
       not_9_out, not_10_out, not_11_out, not_12_out, not_13_out, not_14_out, not_15_out, not_16_out,
       not_17_out, not_18_out, not_19_out, not_20_out, not_21_out, not_22_out, not_23_out, not_24_out,
       not_26_out, not_27_out, not_28_out, not_29_out, not_30_out, not_31_out, not_32_out, not_33_out,
       or_1_out, or_3_out, or_4_out, or_6_out;
  wire [0:0] not_25_out, or_2_out, or_5_out;
  wire [2:0] and_16_out, and_17_out, and_18_out, and_19_out, and_20_out, and_21_out, xor_1_out, xor_2_out;
  wire [2:2] and_10_out, and_11_out, and_12_out, and_13_out, and_14_out, and_27_out, or_7_out, or_8_out;
  wire [3:0] and_1_out;
  wire [3:3] not_1_out;

  not not_1 (not_1_out[3], reset);
  assign and_1_out = {4{Execute}} & Opcode__IR & {4{not_1_out[3]}} & {4{clock}};  // And and_1, 4 bits wide
  not not_2 (not_2_out, and_1_out[2]);
  not not_3 (not_3_out, and_1_out[3]);
  not not_4 (not_4_out, and_1_out[1]);
  not not_5 (not_5_out, and_1_out[0]);
  not not_6 (not_6_out, and_1_out[2]);
  not not_7 (not_7_out, and_1_out[1]);
  not not_8 (not_8_out, and_1_out[3]);
  not not_9 (not_9_out, and_1_out[0]);
  not not_10 (not_10_out, and_1_out[3]);
  not not_11 (not_11_out, and_1_out[3]);
  not not_12 (not_12_out, and_1_out[0]);
  not not_13 (not_13_out, and_1_out[1]);
  not not_14 (not_14_out, and_1_out[2]);
  not not_15 (not_15_out, and_1_out[0]);
  and and_2 (and_2_out, not_15_out, and_1_out[1], not_2_out, not_3_out);
  and and_3 (MOV[1], not_4_out, not_5_out, not_6_out);
  or or_1 (or_1_out, and_1_out[0], and_1_out[1], and_1_out[2], and_1_out[3]);
  and and_4 (and_4_out, and_1_out[0], not_7_out, not_8_out);
  and and_5 (and_5_out, not_9_out, and_1_out[1], not_10_out);
  and and_6 (and_6_out, and_1_out[0], and_1_out[1], and_1_out[2], not_11_out);
  and and_7 (and_7_out, not_12_out, not_13_out, not_14_out, and_1_out[3]);
  and and_8 (MOV[0], and_1_out[0], and_1_out[1], and_1_out[2]);
  or or_2 (or_2_out[0], and_1_out[0], and_1_out[1], and_1_out[2], and_1_out[3]);
  not not_16 (not_16_out, and_1_out[1]);
  not not_17 (not_17_out, and_1_out[2]);
  not not_18 (not_18_out, and_1_out[0]);
  not not_19 (not_19_out, and_1_out[2]);
  not not_20 (not_20_out, and_1_out[2]);
  not not_21 (not_21_out, and_1_out[0]);
  not not_22 (not_22_out, and_1_out[1]);
  not not_23 (not_23_out, and_1_out[1]);
  not not_24 (not_24_out, and_1_out[0]);
  or or_3 (or_3_out, and_6_out, and_7_out);
  or or_4 (or_4_out, MOV[1], MOV[0]);
  or or_5 (or_5_out[0], and_2_out, MOV[1]);
  or or_6 (or_6_out, and_4_out, and_5_out);
  and and_9 (and_9_out, and_1_out[0], not_16_out, not_17_out, and_1_out[3]);
  and and_10 (and_10_out[2], not_18_out, and_1_out[1], not_19_out, and_1_out[3]);
  and and_11 (and_11_out[2], and_1_out[0], and_1_out[1], not_20_out, and_1_out[3]);
  and and_12 (and_12_out[2], not_21_out, not_22_out, and_1_out[2], and_1_out[3]);
  and and_13 (and_13_out[2], and_1_out[0], not_23_out, and_1_out[2], and_1_out[3]);
  and and_14 (and_14_out[2], not_24_out, and_1_out[1], and_1_out[2], and_1_out[3]);
  and and_15 (and_15_out, or_3_out, or_4_out);
  not not_25 (not_25_out[0], and_1_out[3]);
  or or_7 (or_7_out[2], and_9_out, and_15_out);
  assign and_16_out = 3'b000 & {3{or_7_out[2]}};  // And and_16, 3 bits wide
  assign and_17_out = 3'b001 & {3{and_10_out[2]}};  // And and_17, 3 bits wide
  assign and_18_out = 3'b010 & {3{and_11_out[2]}};  // And and_18, 3 bits wide
  assign and_19_out = 3'b011 & {3{and_12_out[2]}};  // And and_19, 3 bits wide
  assign and_20_out = 3'b100 & {3{and_13_out[2]}};  // And and_20, 3 bits wide
  assign and_21_out = 3'b101 & {3{and_14_out[2]}};  // And and_21, 3 bits wide
  assign Write_Reg = {2{Execute}} & {1'b0, or_5_out[0]};  // And and_22, 2 bits wide
  and and_23 (Write_Enabled, or_1_out, Execute);
  assign Read_Reg_1 = {1'b0, not_25_out[0]} & {2{Execute}};  // And and_24, 2 bits wide
  assign Read_Reg_2 = {1'b0, or_2_out[0]} & {2{Execute}};  // And and_25, 2 bits wide
  finiteStateMachine finitestatemachine_1 (.Input(1'b1), .Clock(clock), .MSB(finitestatemachine_1_msb), .LSB(Execute));
  assign xor_1_out = and_16_out ^ and_17_out ^ and_18_out ^ and_19_out ^ and_20_out ^ and_21_out;  // XOr xor_1, 3 bits wide
  and and_26 (Immediate_Load, Execute, or_6_out);
  not not_26 (not_26_out, or_7_out[2]);
  not not_27 (not_27_out, and_10_out[2]);
  not not_28 (not_28_out, and_11_out[2]);
  not not_29 (not_29_out, and_12_out[2]);
  not not_30 (not_30_out, and_13_out[2]);
  not not_31 (not_31_out, and_14_out[2]);
  and and_27 (and_27_out[2], not_26_out, not_27_out, not_28_out, not_29_out, not_30_out, not_31_out);
  and and_28 (Fetch_Enable, not_32_out, not_33_out);
  not not_32 (not_32_out, finitestatemachine_1_msb);
  not not_33 (not_33_out, Execute);
  or or_8 (or_8_out[2], Execute, Fetch_Enable, finitestatemachine_1_msb);
  assign xor_2_out = xor_1_out ^ {3{and_27_out[2]}};  // XOr xor_2, 3 bits wide
  assign ALU_Op = {3{or_8_out[2]}} & xor_2_out;  // And and_29, 3 bits wide

  assign Increment = Fetch_Enable;
  assign Zero_Flag_2 = Zero_flag;
endmodule
