// Digital circuit Classpaticipationcircuit.dig as structural Verilog
module Classpaticipationcircuit (
  input  Input,
  input  clk,
  output MSB,
  output LSB
);

  wire and_1_out, and_2_out, and_3_out, and_4_out, not_1_out, not_2_out, not_3_out, not_4_out, or_1_out,
       or_2_out;

  not not_1 (not_1_out, Input);
  not not_2 (not_2_out, Input);
  not not_3 (not_3_out, LSB);
  not not_4 (not_4_out, MSB);
  and and_1 (and_1_out, Input, LSB);
  and and_2 (and_2_out, not_1_out, MSB);
  and and_3 (and_3_out, LSB, not_2_out);
  and and_4 (and_4_out, not_3_out, not_4_out, Input);
  or or_1 (or_1_out, and_1_out, and_2_out);
  or or_2 (or_2_out, and_3_out, and_4_out);
  D_FF d_ff_1 (.D(or_1_out), .C(clk), .Q(MSB));  // open: nQ
  D_FF d_ff_2 (.D(or_2_out), .C(clk), .Q(LSB));  // open: nQ
endmodule
