// Digital circuit Exception Handler (IR).dig as structural Verilog
module Exception_Handler__IR (
  input  Write_Enable,
  input  [3:0] Opcode_IR,
  output Enable
);

  wire and_1_out, and_2_out, and_3_out, and_4_out, and_5_out, not_1_out, not_2_out, not_3_out, not_4_out,
       not_5_out, not_6_out, not_7_out, not_8_out, not_9_out, not_10_out, or_1_out;

  not not_1 (not_1_out, Opcode_IR[2]);
  not not_2 (not_2_out, Opcode_IR[3]);
  not not_3 (not_3_out, Opcode_IR[0]);
  not not_4 (not_4_out, Opcode_IR[1]);
  not not_5 (not_5_out, Opcode_IR[3]);
  not not_6 (not_6_out, Opcode_IR[1]);
  not not_7 (not_7_out, Opcode_IR[3]);
  not not_8 (not_8_out, Opcode_IR[0]);
  not not_9 (not_9_out, Opcode_IR[3]);
  and and_1 (and_1_out, Opcode_IR[0], Opcode_IR[1], not_1_out, not_2_out);
  and and_2 (and_2_out, not_3_out, not_4_out, Opcode_IR[2], not_5_out);
  and and_3 (and_3_out, Opcode_IR[0], not_6_out, Opcode_IR[2], not_7_out);
  and and_4 (and_4_out, not_8_out, Opcode_IR[1], Opcode_IR[2], not_9_out);
  and and_5 (and_5_out, Opcode_IR[0], Opcode_IR[1], Opcode_IR[2], Opcode_IR[3]);
  or or_1 (or_1_out, and_1_out, and_2_out, and_3_out, and_4_out, and_5_out);
  not not_10 (not_10_out, or_1_out);
  and and_6 (Enable, Write_Enable, not_10_out);
endmodule
