// Digital circuit IR_decoder.dig as structural Verilog
module IR_decoder (
  input  [3:0] IR,
  output [2:0] ALU
);

  wire not_1_out, not_2_out, not_3_out, not_4_out, not_5_out, not_6_out, not_7_out, not_8_out, not_9_out,
       not_10_out, not_11_out, not_12_out, not_13_out, not_14_out, not_15_out;
  wire [2:0] and_2_out, and_3_out, and_5_out, and_7_out, and_8_out, and_9_out, and_10_out, and_11_out,
       and_12_out, not_16_out, xor_1_out;
  wire [2:1] and_4_out, and_6_out;
  wire [2:2] and_1_out, xnor_1_out;

  not not_1 (not_1_out, IR[0]);
  not not_2 (not_2_out, IR[2]);
  not not_3 (not_3_out, IR[3]);
  not not_4 (not_4_out, IR[2]);
  not not_5 (not_5_out, IR[3]);
  not not_6 (not_6_out, IR[0]);
  not not_7 (not_7_out, IR[1]);
  not not_8 (not_8_out, IR[3]);
  not not_9 (not_9_out, IR[1]);
  not not_10 (not_10_out, IR[3]);
  not not_11 (not_11_out, IR[0]);
  not not_12 (not_12_out, IR[3]);
  and and_1 (and_1_out[2], IR[0], not_13_out, not_14_out, not_15_out);
  not not_13 (not_13_out, IR[1]);
  not not_14 (not_14_out, IR[2]);
  not not_15 (not_15_out, IR[3]);
  and and_2 (and_2_out[0], not_1_out, IR[1], not_2_out, not_3_out);
  and and_3 (and_3_out[1], IR[0], IR[1], not_4_out, not_5_out);
  and and_4 (and_4_out[1], not_6_out, not_7_out, IR[2], not_8_out);
  and and_5 (and_5_out[2], IR[0], not_9_out, IR[2], not_10_out);
  and and_6 (and_6_out[2], not_11_out, IR[1], IR[2], not_12_out);
  not not_16 (not_16_out[0], and_1_out[2]);
  not not_17 (not_16_out[1], and_1_out[2]);
  not not_18 (not_16_out[2], and_1_out[2]);
  assign and_7_out = not_16_out & {3{and_1_out[2]}};  // And and_7, 3 bits wide
  not not_19 (and_2_out[1], and_2_out[0]);
  not not_20 (and_2_out[2], and_2_out[0]);
  not not_21 (and_3_out[0], and_3_out[1]);
  not not_22 (and_3_out[2], and_3_out[1]);
  not not_23 (and_4_out[2], and_4_out[1]);
  not not_24 (and_5_out[0], and_5_out[2]);
  not not_25 (and_5_out[1], and_5_out[2]);
  not not_26 (and_6_out[1], and_6_out[2]);
  assign and_8_out = and_2_out & {3{and_2_out[0]}};  // And and_8, 3 bits wide
  assign and_9_out = and_3_out & {3{and_3_out[1]}};  // And and_9, 3 bits wide
  assign and_10_out = {and_4_out, and_4_out[1]} & {3{and_4_out[1]}};  // And and_10, 3 bits wide
  assign and_11_out = and_5_out & {3{and_5_out[2]}};  // And and_11, 3 bits wide
  assign and_12_out = {and_6_out, and_6_out[2]} & {3{and_6_out[2]}};  // And and_12, 3 bits wide
  xnor xnor_1 (xnor_1_out[2], and_1_out[2], and_2_out[0], and_3_out[1], and_4_out[1], and_5_out[2], and_6_out[2]);
  assign xor_1_out = and_7_out ^ and_8_out ^ and_9_out ^ and_10_out ^ and_11_out ^ and_12_out;  // XOr xor_1, 3 bits wide
  assign ALU = xor_1_out ^ {3{xnor_1_out[2]}};  // XOr xor_2, 3 bits wide
endmodule
