// Digital circuit Unimplemented Opcode Blocker.dig as structural Verilog
module Unimplemented_Opcode_Blocker (
  input  [3:0] IR,
  input  Write_Enable,
  output Write_Enable_2
);

  wire and_1_out, and_2_out, and_3_out, and_4_out, nand_1_out, not_1_out, not_2_out, not_3_out, not_4_out,
       not_5_out, not_6_out, not_7_out, not_8_out, not_9_out, or_1_out;

  not not_1 (not_1_out, IR[2]);
  not not_2 (not_2_out, IR[3]);
  not not_3 (not_3_out, IR[0]);
  not not_4 (not_4_out, IR[1]);
  not not_5 (not_5_out, IR[3]);
  not not_6 (not_6_out, IR[1]);
  not not_7 (not_7_out, IR[3]);
  not not_8 (not_8_out, IR[0]);
  not not_9 (not_9_out, IR[3]);
  and and_1 (and_1_out, IR[0], IR[1], not_1_out, not_2_out);
  and and_2 (and_2_out, not_3_out, not_4_out, IR[2], not_5_out);
  and and_3 (and_3_out, IR[0], not_6_out, IR[2], not_7_out);
  and and_4 (and_4_out, not_8_out, IR[1], IR[2], not_9_out);
  or or_1 (or_1_out, and_1_out, and_2_out, and_3_out, and_4_out);
  nand nand_1 (nand_1_out, or_1_out, Write_Enable);
  and and_5 (Write_Enable_2, nand_1_out, Write_Enable);
endmodule
