// Digital circuit complete_CPU.dig as structural Verilog
module complete_CPU (
  input  System_Clock,
  input  Clear_Memory,
  input  Clear_Reg_Data,
  output Less_Than_Flag,
  output Over_Underflow,
  output Zero_Flag
);

  wire _4bit_alu_dlogic_1_overflow, _4bit_alu_dlogic_1_underflow, _4bit_alu_dlogic_1_zero_flag,
       cu_1_fetch_enable, cu_1_immediate_load, cu_1_increment, cu_1_write_enabled,
       exception_handler__ir_1_enable, programcounter_1_out_of_range;
  wire [1:0] cu_1_mov, cu_1_read_reg_1, cu_1_read_reg_2, cu_1_write_reg;
  wire [2:0] cu_1_alu_op;
  wire [3:0] _4bit_alu_dlogic_1_result, _4bit_instruction_register_1_address_bus,
       _4bit_registerfilealu_1_read_data_1, _4bit_registerfilealu_1_read_data_2, memory_module_1_output,
       multiplexer_1_out, programcounter_1_address_bus;

  programCounter programcounter_1 (
    .Load(_4bit_instruction_register_1_address_bus), .Increment(cu_1_increment), .Clock(System_Clock),
    .R_W(cu_1_fetch_enable), .Clear(Clear_Memory), .Address_bus(programcounter_1_address_bus),
    .Out_of_range(programcounter_1_out_of_range));
  Multiplexer #(.Bits(4)) multiplexer_1 (
    .sel(cu_1_immediate_load), .in_0(_4bit_alu_dlogic_1_result),
    .in_1(_4bit_instruction_register_1_address_bus), .out(multiplexer_1_out));
  _4bit_registerFileALU _4bit_registerfilealu_1 (
    .Write_Register(cu_1_write_reg), .Read_Register_1(cu_1_read_reg_1), .Read_Register_2(cu_1_read_reg_2),
    .Write_Data(multiplexer_1_out), .Clock(System_Clock), .Clear(Clear_Reg_Data),
    .R_W(exception_handler__ir_1_enable), .Read_Data_1(_4bit_registerfilealu_1_read_data_1),
    .Read_data_2(_4bit_registerfilealu_1_read_data_2));
  memory_Module memory_module_1 (
    .Clear(Clear_Memory), .Clock(System_Clock), .Data(programcounter_1_address_bus), .R_W(1'b1),
    .Address(programcounter_1_address_bus), .Output(memory_module_1_output));
  _4bit_ALU_dlogic _4bit_alu_dlogic_1 (
    .A(_4bit_registerfilealu_1_read_data_1), .B(_4bit_registerfilealu_1_read_data_2), .Control(cu_1_alu_op),
    .zero(1'b0), .MOV(cu_1_mov), .Result(_4bit_alu_dlogic_1_result),
    .Zero_Flag(_4bit_alu_dlogic_1_zero_flag), .overflow(_4bit_alu_dlogic_1_overflow),
    .Less_Than_Flag(Less_Than_Flag), .underflow(_4bit_alu_dlogic_1_underflow));
  _4bit_Instruction_Register _4bit_instruction_register_1 (
    .Data(memory_module_1_output), .Clock(System_Clock), .Clear(Clear_Memory), .R_W(1'b1),
    .Address_Bus(_4bit_instruction_register_1_address_bus));  // open: ALU_Op
  CU cu_1 (
    .Opcode__IR(_4bit_instruction_register_1_address_bus), .Zero_flag(_4bit_alu_dlogic_1_zero_flag),
    .reset(programcounter_1_out_of_range), .clock(System_Clock), .ALU_Op(cu_1_alu_op),
    .Read_Reg_1(cu_1_read_reg_1), .Read_Reg_2(cu_1_read_reg_2), .Write_Reg(cu_1_write_reg),
    .Write_Enabled(cu_1_write_enabled), .Immediate_Load(cu_1_immediate_load), .Increment(cu_1_increment),
    .Fetch_Enable(cu_1_fetch_enable), .Zero_Flag_2(Zero_Flag), .MOV(cu_1_mov));  // open: Execute
  or or_1 (Over_Underflow, _4bit_alu_dlogic_1_overflow, _4bit_alu_dlogic_1_underflow);
  Exception_Handler__IR exception_handler__ir_1 (
    .Write_Enable(cu_1_write_enabled), .Opcode_IR(_4bit_instruction_register_1_address_bus),
    .Enable(exception_handler__ir_1_enable));
endmodule
