// Digital circuit memory_Module.dig as structural Verilog
module memory_Module (
  input  Clear,
  input  Clock,
  input  [3:0] Data,
  input  R_W,
  input  [3:0] Address,
  output [3:0] Output
);

  wire demultiplexer_1_out_0, demultiplexer_1_out_1, demultiplexer_1_out_2, demultiplexer_1_out_3,
       demultiplexer_1_out_4, demultiplexer_1_out_5, demultiplexer_1_out_6, demultiplexer_1_out_7,
       demultiplexer_1_out_8, demultiplexer_1_out_9, demultiplexer_1_out_10, demultiplexer_1_out_11,
       demultiplexer_1_out_12, demultiplexer_1_out_13, demultiplexer_1_out_14, demultiplexer_1_out_15;
  wire [3:0] Register_0_out, Register_1_out, Register_2_out, Register_3_out, Register_4_out, Register_5_out,
       Register_6_out, Register_7_out, Register_8_out, Register_9_out, Register_10_out, Register_11_out,
       Register_12_out, Register_13_out, Register_14_out, Register_15_out;

  Demultiplexer #(.Selector_Bits(4)) demultiplexer_1 (
    .sel(Address), .in(R_W), .out_0(demultiplexer_1_out_0), .out_1(demultiplexer_1_out_1),
    .out_2(demultiplexer_1_out_2), .out_3(demultiplexer_1_out_3), .out_4(demultiplexer_1_out_4),
    .out_5(demultiplexer_1_out_5), .out_6(demultiplexer_1_out_6), .out_7(demultiplexer_1_out_7),
    .out_8(demultiplexer_1_out_8), .out_9(demultiplexer_1_out_9), .out_10(demultiplexer_1_out_10),
    .out_11(demultiplexer_1_out_11), .out_12(demultiplexer_1_out_12), .out_13(demultiplexer_1_out_13),
    .out_14(demultiplexer_1_out_14), .out_15(demultiplexer_1_out_15));
  _4_bit_register Register_0 (
    .Data(Data), .Clock(Clock), .Clear(Clear), .R_W(demultiplexer_1_out_0), .Out(Register_0_out));
  _4_bit_register Register_1 (
    .Data(Data), .Clock(Clock), .Clear(Clear), .R_W(demultiplexer_1_out_1), .Out(Register_1_out));
  _4_bit_register Register_2 (
    .Data(Data), .Clock(Clock), .Clear(Clear), .R_W(demultiplexer_1_out_2), .Out(Register_2_out));
  _4_bit_register Register_3 (
    .Data(Data), .Clock(Clock), .Clear(Clear), .R_W(demultiplexer_1_out_3), .Out(Register_3_out));
  _4_bit_register Register_4 (
    .Data(Data), .Clock(Clock), .Clear(Clear), .R_W(demultiplexer_1_out_4), .Out(Register_4_out));
  _4_bit_register Register_5 (
    .Data(Data), .Clock(Clock), .Clear(Clear), .R_W(demultiplexer_1_out_5), .Out(Register_5_out));
  _4_bit_register Register_6 (
    .Data(Data), .Clock(Clock), .Clear(Clear), .R_W(demultiplexer_1_out_6), .Out(Register_6_out));
  _4_bit_register Register_7 (
    .Data(Data), .Clock(Clock), .Clear(Clear), .R_W(demultiplexer_1_out_7), .Out(Register_7_out));
  _4_bit_register Register_8 (
    .Data(Data), .Clock(Clock), .Clear(Clear), .R_W(demultiplexer_1_out_8), .Out(Register_8_out));
  _4_bit_register Register_9 (
    .Data(Data), .Clock(Clock), .Clear(Clear), .R_W(demultiplexer_1_out_9), .Out(Register_9_out));
  _4_bit_register Register_10 (
    .Data(Data), .Clock(Clock), .Clear(Clear), .R_W(demultiplexer_1_out_10), .Out(Register_10_out));
  _4_bit_register Register_11 (
    .Data(Data), .Clock(Clock), .Clear(Clear), .R_W(demultiplexer_1_out_11), .Out(Register_11_out));
  _4_bit_register Register_12 (
    .Data(Data), .Clock(Clock), .Clear(Clear), .R_W(demultiplexer_1_out_12), .Out(Register_12_out));
  _4_bit_register Register_13 (
    .Data(Data), .Clock(Clock), .Clear(Clear), .R_W(demultiplexer_1_out_13), .Out(Register_13_out));
  _4_bit_register Register_14 (
    .Data(Data), .Clock(Clock), .Clear(Clear), .R_W(demultiplexer_1_out_14), .Out(Register_14_out));
  _4_bit_register Register_15 (
    .Data(Data), .Clock(Clock), .Clear(Clear), .R_W(demultiplexer_1_out_15), .Out(Register_15_out));
  Multiplexer #(.Selector_Bits(4), .Bits(4)) multiplexer_1 (
    .sel(Address), .in_0(Register_0_out), .in_1(Register_1_out), .in_2(Register_2_out),
    .in_3(Register_3_out), .in_4(Register_4_out), .in_5(Register_5_out), .in_6(Register_6_out),
    .in_7(Register_7_out), .in_8(Register_8_out), .in_9(Register_9_out), .in_10(Register_10_out),
    .in_11(Register_11_out), .in_12(Register_12_out), .in_13(Register_13_out), .in_14(Register_14_out),
    .in_15(Register_15_out), .out(Output));
endmodule
