// Digital circuit part1_steps3&4_(programCounter&IR).dig as structural Verilog
module part1_steps3_4__programCounter_IR (
  input  increment,
  input  clk,
  input  [3:0] Address,
  input  Clear,
  input  R_W,
  input  [3:0] Data_In__To_Mem,
  output [3:0] DataOut__To_CU,
  output reset_flag
);

  wire [3:0] memory_module_1_output, programcounter_1_address_bus;

  programCounter programcounter_1 (
    .Load(Address), .Increment(increment), .Address_bus(programcounter_1_address_bus),
    .Out_of_range(reset_flag));  // open: Clock, R_W, Clear
  memory_Module memory_module_1 (
    .Clear(Clear), .Clock(clk), .Data(Data_In__To_Mem), .R_W(R_W), .Address(programcounter_1_address_bus),
    .Output(memory_module_1_output));
  // _4bit_Instruction_Register _4bit_instruction_register_1: pin names not known; wires that end beside it: memory_module_1_output, clk, Clear, R_W, DataOut__To_CU
endmodule
