// Digital circuit programCounter.dig as structural Verilog
module programCounter (
  input  [3:0] Load,
  input  Increment,
  input  Clock,
  input  R_W,
  input  Clear,
  output [3:0] Address_bus,
  output Out_of_range
);

  wire [3:0] _4bit_full_adder_1_p4;

  // _4bit_full_adder _4bit_full_adder_1: pin names not known; wires that end beside it: 1'b0, Load, {3'b000, Increment}, _4bit_full_adder_1_p4, Out_of_range
  _4_bit_register _4_bit_register_1 (
    .Data(_4bit_full_adder_1_p4), .Clock(Clock), .Clear(Clear), .R_W(R_W), .Out(Address_bus));
endmodule
